# Fritzing sketch portcullis (saved by Fritzing 1.0.3b)
circuit board: 2.99999cm x 11cm
breadboards: 2

parts:
  100K = Rotary Potentiometer (Small) [maximum_resistance=100kΩ knob_status=50% power=0.5W package=THT]
  100K_2 = Rotary Potentiometer (Small) [maximum_resistance=100kΩ knob_status=50% power=0.5W package=THT]
  100K_3 = Rotary Potentiometer (Small) [maximum_resistance=100kΩ knob_status=50% power=0.5W package=THT]
  100K_4 = Resistor [tolerance=±5% resistance=100k power=0.25W package=THT]
  1K = Resistor [tolerance=±5% resistance=1k power=0.25W package=THT]
  072 = TL072 [package="DIP (Dual Inline) [THT]"]
  072_PWR = TL072 [package="DIP (Dual Inline) [THT]"]
  072_A = TL072 [package="DIP (Dual Inline) [THT]"]
  072_B = TL072 [package="DIP (Dual Inline) [THT]"]  # not connected
  IN = PJ-301M [part_number=PJ-301M]
  103 = Ceramic Capacitor [capacitance=10nF voltage=16V package="200 mil [THT, multilayer]"]
  104 = Ceramic Capacitor [capacitance=100nF voltage=16V package="200 mil [THT, multilayer]"]
  J3 = shrouded pin header, 16 pins [form="♂ (shrouded male)"]
  5||12 = SPST Switch [package=switch-spdt_kit]
  103_2 = Ceramic Capacitor [capacitance=10nF voltage=16V package="200 mil [THT, multilayer]"]
  100K1 = Resistor [tolerance=±5% resistance=100k power=0.25W package=THT]
  103_3 = Ceramic Capacitor [capacitance=10nF voltage=16V package="200 mil [THT, multilayer]"]
  5817 = Diode [package=diode-1n4148]
  100uF = Electrolytic Capacitor [capacitance=0.1mF voltage=35V package="100 mil [THT, electrolytic]"]
  IN1 = PJ-301M [part_number=PJ-301M]
  IN2 = PJ-301M [part_number=PJ-301M]
  IN3 = PJ-301M [part_number=PJ-301M]
  IN4 = PJ-301M [part_number=PJ-301M]
  IN5 = PJ-301M [part_number=PJ-301M]
  IN6 = PJ-301M [part_number=PJ-301M]
  out = PJ-301M [part_number=PJ-301M]
  S1 = Taiway 100-SP-X-T1 SPDT Miniature Toggle Switch [part_number=100-SP-X-T1-0-0-B1-M2 package=THT]
  1uF = Electrolytic Capacitor [capacitance=1µF voltage=35V package="100 mil [THT, electrolytic]"]
  10uF = Electrolytic Capacitor [capacitance=10µF voltage=35V package="100 mil [THT, electrolytic]"]
  1K1 = Resistor [tolerance=±5% power=0.25W resistance=1k package=THT]
  1K_2 = Resistor [tolerance=±5% power=0.25W resistance=1k package=THT]
  1K_3 = Resistor [tolerance=±5% power=0.25W resistance=1k package=THT]
  100nF = Film/Foil Capacitor [capacitance=100nF voltage=35V package="5mm [THT, pp]"]
  100nF_2 = Film/Foil Capacitor [capacitance=100nF voltage=35V package="5mm [THT, pp]"]
  100nF_3 = Film/Foil Capacitor [capacitance=100nF voltage=35V package="5mm [THT, pp]"]
  100nF_4 = Film/Foil Capacitor [capacitance=100nF voltage=35V package="5mm [THT, pp]"]
  100nF_5 = Film/Foil Capacitor [capacitance=100nF voltage=35V package="5mm [THT, pp]"]
  100nF_6 = Film/Foil Capacitor [capacitance=100nF voltage=35V package="5mm [THT, pp]"]

nets:
  N1: 100K.leg1, IN5.Pin_2, IN5.Pin_3, 100nF_4.-
  N2: 100K.wiper, 1K_2.Pin_0
  N3: 100K.leg2, IN3.Pin_2, IN3.Pin_3, 100nF_3.-
  N4: 100K_2.leg1, IN2.Pin_2, IN2.Pin_3, 100nF_2.-
  N5: 100K_2.wiper, 1K1.Pin_0
  N6: 100K_2.leg2, IN1.Pin_2, IN1.Pin_3, 100nF.-
  N7: 100K_3.leg1, IN6.Pin_2, IN6.Pin_3, 100nF_6.-
  N8: 100K_3.wiper, 1K_3.Pin_0
  N9: 100K_3.leg2, IN4.Pin_2, IN4.Pin_3, 100nF_5.-
  N10: 100K_4.Pin_0, 1K.Pin_1, 072.connector2, 072_A.pin3
  N11: 100K_4.Pin_1, 103.0, 104.0, 5||12.P, 103_2.0, 103_3.0, 100uF.+
  GND: 1K.Pin_0, 072.connector3, 072_PWR.pin4, IN.Pin_1, 104.1, J3.pin2, J3.pin3, J3.pin4, J3.pin13, J3.pin14, J3.pin15, 100K1.Pin_1, 100uF.-, IN1.Pin_1, IN2.Pin_1, IN3.Pin_1, IN4.Pin_1, IN5.Pin_1, IN6.Pin_1, out.Pin_1, S1.COM, 1uF.-, 10uF.-
  N12: 072.connector0, 072_A.pin1, 5817.A
  N13: 072.connector1, 072_A.pin2, IN.Pin_3, 100K1.Pin_0
  N14: 072.connector7, 072_PWR.pin8, 103.1
  N15: J3.pin1, J3.pin16
  9V: J3.pin5, J3.pin6, J3.pin11, J3.pin12, 5||12.O, 5||12.S
  N16: J3.pin7, J3.pin10
  N17: J3.pin8, J3.pin9
  N18: out.Pin_3, 1K1.Pin_1, 1K_2.Pin_1, 1K_3.Pin_1
  N19: S1.L1, 10uF.+
  N20: S1.L2, 1uF.+

notes:
  the rack
  blueprint@poetaster . de 2025

custom parts:
  TL072: Dual Operational Amplifier
  TL072: Dual Operational Amplifier
  TL072: Dual Operational Amplifier
  TL072: Dual Operational Amplifier
  PJ-301M: Phone power jack.
